// Logisim project SPM8_8.circ as structural Verilog: 1 circuit, main circuit main
module main (
  input  x7,
  input  x6,
  input  x5,
  input  x4,
  input  x3,
  input  x2,
  input  x1,
  input  x0,
  input  y,
  input  R,
  output Prod
);

  wire and_1_out, and_2_out, and_3_out, and_4_out, and_5_out, and_6_out, and_7_out, and_8_out, csa_1_pp,
       csa_2_pp, csa_3_pp, csa_4_pp, csa_5_pp, csa_6_pp, csa_7_pp;

  and and_1 (and_1_out, y, x7);
  and and_2 (and_2_out, y, x6);
  and and_3 (and_3_out, y, x5);
  CSA csa_1 (.x(and_1_out), .y(1'b0), .R(R), .pp(csa_1_pp));
  and and_4 (and_4_out, y, x4);
  and and_5 (and_5_out, y, x3);
  CSA csa_2 (.x(and_2_out), .y(csa_1_pp), .R(R), .pp(csa_2_pp));
  and and_6 (and_6_out, y, x2);
  and and_7 (and_7_out, y, x1);
  CSA csa_3 (.x(and_3_out), .y(csa_2_pp), .R(R), .pp(csa_3_pp));
  and and_8 (and_8_out, y, x0);
  CSA csa_4 (.x(and_4_out), .y(csa_3_pp), .R(R), .pp(csa_4_pp));
  CSA csa_5 (.x(and_5_out), .y(csa_4_pp), .R(R), .pp(csa_5_pp));
  CSA csa_6 (.x(and_6_out), .y(csa_5_pp), .R(R), .pp(csa_6_pp));
  CSA csa_7 (.x(and_7_out), .y(csa_6_pp), .R(R), .pp(csa_7_pp));
  CSA csa_8 (.x(and_8_out), .y(csa_7_pp), .R(R), .pp(Prod));
endmodule
