// Logisim project carry_save_adder.circ as structural Verilog: 1 circuit, main circuit CSA
module CSA (
  input  x,
  input  y,
  input  R,
  output pp
);

  wire adder_1_cout, adder_1_out, and_1_out, and_2_out, CLK_out, d_ff_2_q, nor_1_out, not_1_out, not_2_out,
       xor_1_out;

  xor xor_1 (xor_1_out, x, adder_1_out);
  Clock CLK (.out(CLK_out));
  and and_1 (and_1_out, x, adder_1_out);
  D_Flip_Flop d_ff_1 (.D(xor_1_out), .clk(CLK_out), .Q(pp), .reset(not_1_out));  // open: Qn, preset
  not not_1 (not_1_out, R);
  Adder #(.width(1)) adder_1 (.a(y), .b(d_ff_2_q), .out(adder_1_out), .cin(1'b0), .cout(adder_1_cout));
  and and_2 (and_2_out, and_1_out, adder_1_cout);
  D_Flip_Flop d_ff_2 (.D(nor_1_out), .clk(CLK_out), .Q(d_ff_2_q), .reset(not_2_out));  // open: Qn, preset
  nor nor_1 (nor_1_out, and_1_out, adder_1_cout);
  not not_2 (not_2_out, R);

  // Notes on the sheet:
  //   X
  //   Y
  //   R
  //   Clk
  //   Sum
  //   FDHA
endmodule
